// Logisim project Logic_Project.circ as structural Verilog: 2 circuits, main circuit TestBench
module TestBench (
  input  [7:0] Address,
  input  JumpToAddress
);

  wire button_1_out, clock_1_out, comparator_1_eq;
  wire [3:0] rom_1_data_2;
  wire [7:0] alu_1_out_4, counter_1_q;
  wire [15:0] rom_1_data;

  Clock clock_1 (.out(clock_1_out));
  Button button_1 (.out(button_1_out));
  ROM #(.dataWidth(20)) rom_1 (.addr(counter_1_q), .data({rom_1_data_2, rom_1_data}));
  Counter counter_1 (
    .load(JumpToAddress), .D(Address), .count(1'b1), .Q(counter_1_q), .up(1'b1), .clk(clock_1_out),
    .clr(button_1_out));  // open: carry
  Hex_Digit_Display #(.decimalPoint("false")) Operation (.value(rom_1_data_2));
  Hex_Digit_Display #(.decimalPoint("false")) hex_digit_display_1 (.value(rom_1_data[15:12]));
  Hex_Digit_Display #(.decimalPoint("false")) hex_digit_display_2 (.value(rom_1_data[11:8]));
  ALU alu_1 (.in_1(rom_1_data_2), .Operand1(rom_1_data[15:12]), .Operand2(rom_1_data[11:8]), .out_4(alu_1_out_4));
  Hex_Digit_Display #(.decimalPoint("false")) hex_digit_display_3 (.value(alu_1_out_4[7:4]));
  Hex_Digit_Display #(.decimalPoint("false")) hex_digit_display_4 (.value(alu_1_out_4[3:0]));
  LED led_1 (.in(comparator_1_eq));
  Comparator comparator_1 (.a(alu_1_out_4), .b(rom_1_data[7:0]), .eq(comparator_1_eq));  // open: gt, lt

  // Notes on the sheet:
  //   Clock
  //   Restart
  //   contents of rom_1 (hex, n*v repeats v):
  //   a00a 1a0f6 10000 21203 2af19 3fa05 3affb 4340c 4ffe1 8a0f5 800ff 9a302 aa30b ba309 cf00f cf378 cf780
  //   cf800 df00f df301 df400 df800
  //   Operation
  //   Operand 1
  //   Don't Modify This Testbench
  //   Operand 2
  //   Result
  //   OK
endmodule

module ALU (
  input  [3:0] in_1,
  input  [3:0] Operand1,
  input  [3:0] Operand2,
  output [7:0] out_4
);

  // Main_Circuit_6694b15e main_circuit_6694b15e_1: pin names not known; wires that end beside it: in_1[3], in_1[2], in_1[1], Operand1[3], in_1[0], Operand1[2], out_4[7], Operand1[1], out_4[6], Operand1[0], out_4[5], Operand2[3], out_4[4], Operand2[2], out_4[3], Operand2[1], out_4[2], Operand2[0], out_4[1], out_4[0]

  // Notes on the sheet:
  //   Complete This Circuit
endmodule
